# Fritzing sketch .diagram (saved by Fritzing 0.9.3b)
breadboards: 1

parts:
  M1 = FireBeetle ESP32-E
  RCWL-0516_Microwave_Radar_Motion_Sensor1 = RCWL-0516 Microwave Radar Motion Sensor Module
  M2 = FireBeetle ESP32-E
  U1 = L9110 H-bridge module [part_number="L9110 H-bridge"]
  M3 = DC Motor
  VCC1 = 4 x AAA Battery Mount

nets:
  N1: M1.pin_12, M1.pin_20, RCWL-0516_Microwave_Radar_Motion_Sensor1.GND
  N2: M1.pin_14, RCWL-0516_Microwave_Radar_Motion_Sensor1.VIN
  N3: M1.pin_30, RCWL-0516_Microwave_Radar_Motion_Sensor1.OUT
  N4: M2.pin_3, M2.pin_4, M2.pin_5, M2.pin_6, M2.pin_7, M2.pin_9, M2.pin_10, M2.pin_11, M2.pin_12, M2.pin_13, M2.pin_15, M2.pin_16, M2.pin_20, M2.pin_25, M2.pin_26, U1.GND, VCC1.-
  N5: M2.pin_29, U1.B-IB
  N6: M2.pin_30, U1.B-IA
  N7: U1.VCC, VCC1.+
  N8: U1.MOTOR_B-A, M3.pin_2
  N9: U1.MOTOR_B-B, M3.pin_1

notes:
  5v from XY-UP USB Power Supply

custom parts:
  FireBeetle ESP32-E: FireBeetle ESP32-E, specially designed for IoT, is an ESP-WROOM-32E-based main controller board with dual-core chips. It supports WiFi and Bluetooth dual-mode communication and features a small size, ultra-low power consumption, on-board charging circuit, and easy-to-use interface, which can be conveniently used for smart home IoT, industrial IoT applications, wearable devices, and so on. You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
  RCWL-0516 Microwave Radar Motion Sensor Module: The RCWL-0516 is a microwave radar motion sensor module. Input voltage is 4V to 28V. The 3V3 pin is a power output.
